# Fritzing sketch fritzing (saved by Fritzing 0.7.12b)
breadboards: 1

parts:
  Arduino1 = Arduino
  R2 = Rotary Potentiometer (Large) [package=THT]

nets:
  N1: Arduino1.+5V, R2.leg2
  N2: Arduino1.GND, R2.leg1
  N3: Arduino1.A1, R2.wiper
